// Logisim project ALU_v4.circ as structural Verilog: 5 circuits, main circuit main
module main (
  input  A,
  input  B,
  input  Cin,
  output Sum,
  output Cout
);

  wire and_1_out, and_2_out, xor_1_out;

  and and_1 (and_1_out, A, B);
  xor xor_1 (xor_1_out, A, B);
  xor xor_2 (Sum, xor_1_out, Cin);
  and and_2 (and_2_out, xor_1_out, Cin);
  or or_1 (Cout, and_2_out, and_1_out);
endmodule

module _1bit_FA (
  input  S2,
  input  CARRY_prime,
  input  S1,
  input  S0,
  input  A0,
  input  B0,
  input  A1,
  input  B1,
  input  in_9,
  input  in_10,
  input  in_11,
  input  in_12
);

  wire and_1_out, and_2_out, and_3_out, and_4_out, and_5_out, and_6_out, and_7_out, and_8_out, and_9_out,
       and_10_out, and_11_out, and_12_out, and_13_out, and_14_out, and_15_out, and_16_out, and_17_out,
       and_18_out, and_19_out, and_20_out, and_21_out, and_22_out, and_23_out, and_24_out, and_25_out,
       and_26_out, and_27_out, main_1_cout, main_2_cout, main_3_cout, not_1_out, not_2_out, not_3_out,
       not_4_out, not_5_out, not_6_out, not_7_out, not_8_out, or_1_out, or_2_out, or_3_out, or_4_out,
       or_5_out, or_6_out, or_7_out, or_8_out, or_9_out;

  not not_1 (not_1_out, S0);
  not not_2 (not_2_out, S2);
  not not_3 (not_3_out, S1);
  not not_4 (not_4_out, B0);
  not not_5 (not_5_out, B1);
  not not_6 (not_6_out, in_10);
  not not_7 (not_7_out, in_12);
  not not_8 (not_8_out, CARRY_prime);
  and and_1 (and_1_out, B0, S0, not_3_out, S2);
  and and_2 (and_2_out, not_4_out, S0, not_2_out);
  and and_3 (and_3_out, S0, S1, S2);
  and and_4 (and_4_out, not_1_out, not_3_out);
  and and_5 (and_5_out, B1, S0, not_3_out, S2);
  and and_6 (and_6_out, not_5_out, S0, not_2_out);
  and and_7 (and_7_out, S0, S1, S2);
  and and_8 (and_8_out, not_1_out, not_3_out);
  and and_9 (and_9_out, in_10, S0, not_3_out, S2);
  and and_10 (and_10_out, not_6_out, S0, not_2_out);
  and and_11 (and_11_out, S0, S1, S2);
  and and_12 (and_12_out, not_1_out, not_3_out);
  and and_13 (and_13_out, in_12, S0, not_3_out, S2);
  and and_14 (and_14_out, not_7_out, S0, not_2_out);
  and and_15 (and_15_out, S0, S1, S2);
  and and_16 (and_16_out, not_1_out, not_3_out);
  and and_17 (and_17_out, not_8_out, S1, not_2_out);
  and and_18 (and_18_out, not_3_out, not_2_out);
  and and_19 (and_19_out, S1, S2);
  or or_1 (or_1_out, A0, and_20_out);
  and and_20 (and_20_out, not_1_out, S1, B0);
  or or_2 (or_2_out, and_1_out, and_2_out, and_3_out, and_4_out);
  or or_3 (or_3_out, A1, and_21_out);
  and and_21 (and_21_out, not_1_out, S1, B1);
  or or_4 (or_4_out, and_5_out, and_6_out, and_7_out, and_8_out);
  or or_5 (or_5_out, in_9, and_22_out);
  and and_22 (and_22_out, not_1_out, S1, in_10);
  or or_6 (or_6_out, and_9_out, and_10_out, and_11_out, and_12_out);
  or or_7 (or_7_out, in_11, and_23_out);
  and and_23 (and_23_out, not_1_out, S1, in_12);
  or or_8 (or_8_out, and_13_out, and_14_out, and_15_out, and_16_out);
  or or_9 (or_9_out, and_17_out, and_18_out, and_19_out);
  and and_24 (and_24_out, S0, or_9_out);
  main main_1 (.A(or_1_out), .B(or_2_out), .Cin(and_24_out), .Cout(main_1_cout));  // open: Sum
  and and_25 (and_25_out, S0, main_1_cout);
  main main_2 (.A(or_3_out), .B(or_4_out), .Cin(and_25_out), .Cout(main_2_cout));  // open: Sum
  and and_26 (and_26_out, S0, main_2_cout);
  main main_3 (.A(or_5_out), .B(or_6_out), .Cin(and_26_out), .Cout(main_3_cout));  // open: Sum
  and and_27 (and_27_out, S0, main_3_cout);
  main main_4 (.A(or_7_out), .B(or_8_out), .Cin(and_27_out));  // open: Sum, Cout
endmodule

module ALU_IC_sim (
  input  Cin,
  input  S2,
  input  S1,
  input  S0,
  input  A0,
  input  B0,
  input  A1,
  input  B1,
  input  A2,
  input  B2,
  input  A3,
  input  B3,
  output F0,
  output F1,
  output V,
  output Z,
  output C,
  output S,
  output F2,
  output F3
);

  wire ic_7404_1_p5, ic_7404_1_p6, ic_7404_1_p7, ic_7404_1_p8, ic_7404_1_p9, ic_7404_1_p10, ic_7404_2_p5,
       ic_7404_2_p6, ic_7404_2_p7, ic_7404_2_p8, ic_7404_2_p9, ic_7408_1_p9, ic_7408_1_p10, ic_7408_1_p11,
       ic_7408_1_p12, ic_7408_2_p8, ic_7408_2_p9, ic_7408_2_p10, ic_7408_2_p12, ic_7408_3_p6, ic_7408_3_p7,
       ic_7408_3_p8, ic_7408_3_p9, ic_7408_4_p18, ic_7408_4_p19, ic_7408_4_p20, ic_7408_4_p21, ic_7408_5_p9,
       ic_7408_5_p10, ic_7408_5_p11, ic_7408_5_p12, ic_7408_6_p5, ic_7408_6_p6, ic_7408_6_p8, ic_7408_6_p9,
       ic_7408_6_p10, ic_7408_6_p11, ic_7432_1_p5, ic_7432_1_p6, ic_7432_2_p5, ic_7432_2_p6, ic_7432_2_p7,
       ic_7432_2_p8, ic_7432_3_p7, ic_7432_3_p8, ic_7432_3_p9, ic_7432_3_p10, ic_7432_4_p9, ic_7432_4_p10,
       ic_7432_4_p11, ic_7432_4_p12, ic_7432_5_p3, ic_7432_5_p6, ic_7486_1_p2;

  // IC_7404 ic_7404_1: pin names not known; wires that end beside it: S2, S1, S0, Cin, ic_7404_1_p5, ic_7404_1_p6, ic_7404_1_p7, ic_7404_1_p8, ic_7404_1_p9, ic_7404_1_p10
  // IC_7408 ic_7408_1: pin names not known; wires that end beside it: ic_7404_1_p8, S0, ic_7404_1_p8, S0, S1, ic_7404_1_p6, ic_7404_1_p7, S2, ic_7408_1_p9, ic_7408_1_p10, ic_7408_1_p11, ic_7408_1_p12
  // IC_7408 ic_7408_2: pin names not known; wires that end beside it: ic_7408_1_p12, ic_7408_1_p12, S1, ic_7404_1_p9, ic_7404_1_p7, S1, ic_7404_1_p6, ic_7408_2_p8, ic_7408_2_p9, ic_7408_2_p10, ic_7408_2_p8, ic_7408_2_p12
  // IC_7432 ic_7432_1: pin names not known; wires that end beside it: ic_7408_1_p11, ic_7404_1_p10, ic_7408_2_p10, ic_7408_2_p12, ic_7432_1_p5, ic_7432_1_p6
  // IC_7486 ic_7486_1: pin names not known; wires that end beside it: S2, ic_7486_1_p2, S1, C, ic_7404_1_p5, V
  // IC_7404 ic_7404_2: pin names not known; wires that end beside it: B0, B1, B2, B3, ic_7404_2_p5, ic_7404_2_p6, ic_7404_2_p7, ic_7404_2_p8, ic_7404_2_p9, Z
  // IC_7408 ic_7408_3: pin names not known; wires that end beside it: ic_7408_1_p10, ic_7408_1_p10, ic_7408_1_p10, ic_7408_1_p10, ic_7404_2_p6, ic_7408_3_p6, ic_7408_3_p7, ic_7408_3_p8, ic_7408_3_p9
  // IC_7408 ic_7408_4: pin names not known; wires that end beside it: B2, B3, ic_7404_2_p6, ic_7404_2_p7, ic_7404_2_p8, ic_7404_2_p9, ic_7404_2_p7, ic_7404_2_p8, ic_7404_2_p9, ic_7408_2_p9, ic_7408_2_p9, ic_7408_2_p9, ic_7408_2_p9, B0, B1, B2, B3, ic_7408_4_p18, ic_7408_4_p19, ic_7408_4_p20, ic_7408_4_p21, ic_7408_4_p18, ic_7408_4_p19, ic_7408_4_p20, ic_7408_4_p21
  // IC_7408 ic_7408_5: pin names not known; wires that end beside it: ic_7408_1_p9, ic_7408_1_p9, ic_7408_1_p9, ic_7408_1_p9, B0, B1, B2, B3, ic_7408_5_p9, ic_7408_5_p10, ic_7408_5_p11, ic_7408_5_p12
  // IC_7432 ic_7432_2: pin names not known; wires that end beside it: ic_7408_3_p6, ic_7408_3_p7, ic_7408_3_p8, ic_7408_3_p9, ic_7432_2_p5, ic_7432_2_p6, ic_7432_2_p7, ic_7432_2_p8, A2, A3
  // IC_7432 ic_7432_3: pin names not known; wires that end beside it: ic_7408_5_p9, ic_7408_5_p10, ic_7408_5_p11, ic_7408_5_p12, A0, A1, ic_7432_3_p7, ic_7432_3_p8, ic_7432_3_p9, ic_7432_3_p10
  // IC_7432 ic_7432_4: pin names not known; wires that end beside it: ic_7432_2_p5, ic_7432_2_p6, ic_7432_2_p7, ic_7432_2_p8, ic_7432_1_p5, ic_7432_1_p5, ic_7432_1_p5, ic_7432_1_p5, ic_7432_4_p9, ic_7432_4_p10, ic_7432_4_p11, ic_7432_4_p12
  // IC_7408 ic_7408_6: pin names not known; wires that end beside it: S0, S0, S0, S0, ic_7408_6_p5, ic_7408_6_p6, ic_7432_1_p6, ic_7408_6_p8, ic_7408_6_p9, ic_7408_6_p10, ic_7408_6_p11, ic_7486_1_p2
  IC_7483 ic_7483_1 (
    .Cin(ic_7408_6_p11), .A0(ic_7432_3_p7), .B0(ic_7432_4_p9), .A1(1'b0), .B1(1'b0), .A2(ic_7408_6_p9),
    .B2(ic_7408_6_p9), .A3(ic_7432_3_p8), .B3(ic_7432_4_p10), .Y0(F0), .Y1(ic_7408_6_p5), .Y3(F1),
    .Cout(ic_7408_6_p6));  // open: Y2
  IC_7483 ic_7483_2 (
    .Cin(ic_7408_6_p10), .A0(ic_7432_3_p9), .B0(ic_7432_4_p11), .A1(1'b0), .B1(1'b0), .A2(ic_7486_1_p2),
    .B2(ic_7486_1_p2), .A3(ic_7432_3_p10), .B3(ic_7432_4_p12), .Y0(F2), .Y1(ic_7408_6_p8), .Y3(F3), .Cout(C));  // open: Y2
  // IC_7432 ic_7432_5: pin names not known; wires that end beside it: F0, F2, ic_7432_5_p3, F1, F3, ic_7432_5_p6, ic_7432_5_p3, ic_7432_5_p6, ic_7404_2_p5

  assign S = F3;

  // Notes on the sheet:
  //   s0' s1 | s0 s2' | s0' s1' | s0 s2
  //   s0 s1' s2 | s0 s1 s2
  //   s0 s1' s2 | s0's1'+s0s1s2
  //   b' s1 s2'
  //   s0' s1 | s0 s2' |
  //   B's0s2'
  //   Bs0s1's2
  //   x0 x1 x2 x3
  //   y0y1y2y3
  //   Z
endmodule

module IC_7483 (
  input  Cin,
  input  A0,
  input  B0,
  input  A1,
  input  B1,
  input  A2,
  input  B2,
  input  A3,
  input  B3,
  output Y0,
  output Y1,
  output Y2,
  output Y3,
  output Cout
);

  wire main_1_cout, main_2_cout, main_3_cout;

  main main_1 (.A(A0), .B(B0), .Cin(Cin), .Sum(Y0), .Cout(main_1_cout));
  main main_2 (.A(A1), .B(B1), .Cin(main_1_cout), .Sum(Y1), .Cout(main_2_cout));
  main main_3 (.A(A2), .B(B2), .Cin(main_2_cout), .Sum(Y2), .Cout(main_3_cout));
  main main_4 (.A(A3), .B(B3), .Cin(main_3_cout), .Sum(Y3), .Cout(Cout));
endmodule

module ALU_test_ground (
  input  Carry,
  input  S2,
  input  S1,
  input  S0,
  input  A3,
  input  A2,
  input  A1,
  input  A0,
  input  B3,
  input  B2,
  input  B1,
  input  B0,
  output F3,
  output F2,
  output F1,
  output F0,
  output C,
  output S,
  output V,
  output Z
);

  ALU_IC_sim alu_ic_sim_1 (
    .S2(S2), .S1(S1), .S0(S0), .A0(A0), .B0(B0), .A1(A1), .B1(B1), .A2(A2), .B2(B2), .A3(A3), .B3(B3), .Z(Z),
    .Cin(Carry), .C(C), .S(S), .V(V), .F0(F0), .F1(F1), .F2(F2), .F3(F3));
endmodule
