// Logisim project FP-Adder_Tuhin-6.circ as structural Verilog: 15 circuits, main circuit main
module main (
  input  [15:0] Number_A,
  input  [15:0] Number_B,
  input  Add_prime_Sub,
  output [15:0] Number_Sum
);

  Floating_Point_Adder floating_point_adder_1 (
    .Add_prime_Sub(Add_prime_Sub), .Number_A(Number_A), .Number_B(Number_B), .Number_Sum(Number_Sum));
endmodule

module Right_Shifter (
  input  [14:0] Input,
  input  [4:0] Shift_Amount,
  output [14:0] Output
);

  wire or_1_out, or_2_out, or_3_out, or_4_out, or_5_out, or_6_out, or_7_out, or_8_out, or_9_out, or_10_out,
       or_11_out, or_12_out, or_13_out, or_14_out;

  Multiplexer #(.select(5), .disabled(0), .enable("false")) multiplexer_1 (
    .in0(Input[14]), .in1(1'b0), .in2(1'b0), .in3(1'b0), .in4(1'b0), .in5(1'b0), .in6(1'b0), .in7(1'b0),
    .in8(1'b0), .in9(1'b0), .in10(1'b0), .in11(1'b0), .in12(1'b0), .in13(1'b0), .in14(1'b0), .in15(1'b0),
    .in16(1'b0), .in17(1'b0), .in18(1'b0), .in19(1'b0), .in20(1'b0), .in21(1'b0), .in22(1'b0), .in23(1'b0),
    .in24(1'b0), .in25(1'b0), .in26(1'b0), .in27(1'b0), .in28(1'b0), .in29(1'b0), .in30(1'b0), .in31(1'b0),
    .out(Output[14]), .sel(Shift_Amount));
  Multiplexer #(.select(5), .disabled(0), .enable("false")) multiplexer_2 (
    .in0(Input[13]), .in1(Input[14]), .in2(1'b0), .in3(1'b0), .in4(1'b0), .in5(1'b0), .in6(1'b0), .in7(1'b0),
    .in8(1'b0), .in9(1'b0), .in10(1'b0), .in11(1'b0), .in12(1'b0), .in13(1'b0), .in14(1'b0), .in15(1'b0),
    .in16(1'b0), .in17(1'b0), .in18(1'b0), .in19(1'b0), .in20(1'b0), .in21(1'b0), .in22(1'b0), .in23(1'b0),
    .in24(1'b0), .in25(1'b0), .in26(1'b0), .in27(1'b0), .in28(1'b0), .in29(1'b0), .in30(1'b0), .in31(1'b0),
    .out(Output[13]), .sel(Shift_Amount));
  Multiplexer #(.select(5), .disabled(0), .enable("false")) multiplexer_3 (
    .in0(Input[12]), .in1(Input[13]), .in2(Input[14]), .in3(1'b0), .in4(1'b0), .in5(1'b0), .in6(1'b0),
    .in7(1'b0), .in8(1'b0), .in9(1'b0), .in10(1'b0), .in11(1'b0), .in12(1'b0), .in13(1'b0), .in14(1'b0),
    .in15(1'b0), .in16(1'b0), .in17(1'b0), .in18(1'b0), .in19(1'b0), .in20(1'b0), .in21(1'b0), .in22(1'b0),
    .in23(1'b0), .in24(1'b0), .in25(1'b0), .in26(1'b0), .in27(1'b0), .in28(1'b0), .in29(1'b0), .in30(1'b0),
    .in31(1'b0), .out(Output[12]), .sel(Shift_Amount));
  Multiplexer #(.select(5), .disabled(0), .enable("false")) multiplexer_4 (
    .in0(Input[11]), .in1(Input[12]), .in2(Input[13]), .in3(Input[14]), .in4(1'b0), .in5(1'b0), .in6(1'b0),
    .in7(1'b0), .in8(1'b0), .in9(1'b0), .in10(1'b0), .in11(1'b0), .in12(1'b0), .in13(1'b0), .in14(1'b0),
    .in15(1'b0), .in16(1'b0), .in17(1'b0), .in18(1'b0), .in19(1'b0), .in20(1'b0), .in21(1'b0), .in22(1'b0),
    .in23(1'b0), .in24(1'b0), .in25(1'b0), .in26(1'b0), .in27(1'b0), .in28(1'b0), .in29(1'b0), .in30(1'b0),
    .in31(1'b0), .out(Output[11]), .sel(Shift_Amount));
  Multiplexer #(.select(5), .disabled(0), .enable("false")) multiplexer_5 (
    .in0(Input[10]), .in1(Input[11]), .in2(Input[12]), .in3(Input[13]), .in4(Input[14]), .in5(1'b0),
    .in6(1'b0), .in7(1'b0), .in8(1'b0), .in9(1'b0), .in10(1'b0), .in11(1'b0), .in12(1'b0), .in13(1'b0),
    .in14(1'b0), .in15(1'b0), .in16(1'b0), .in17(1'b0), .in18(1'b0), .in19(1'b0), .in20(1'b0), .in21(1'b0),
    .in22(1'b0), .in23(1'b0), .in24(1'b0), .in25(1'b0), .in26(1'b0), .in27(1'b0), .in28(1'b0), .in29(1'b0),
    .in30(1'b0), .in31(1'b0), .out(Output[10]), .sel(Shift_Amount));
  Multiplexer #(.select(5), .disabled(0), .enable("false")) multiplexer_6 (
    .in0(Input[9]), .in1(Input[10]), .in2(Input[11]), .in3(Input[12]), .in4(Input[13]), .in5(Input[14]),
    .in6(1'b0), .in7(1'b0), .in8(1'b0), .in9(1'b0), .in10(1'b0), .in11(1'b0), .in12(1'b0), .in13(1'b0),
    .in14(1'b0), .in15(1'b0), .in16(1'b0), .in17(1'b0), .in18(1'b0), .in19(1'b0), .in20(1'b0), .in21(1'b0),
    .in22(1'b0), .in23(1'b0), .in24(1'b0), .in25(1'b0), .in26(1'b0), .in27(1'b0), .in28(1'b0), .in29(1'b0),
    .in30(1'b0), .in31(1'b0), .out(Output[9]), .sel(Shift_Amount));
  Multiplexer #(.select(5), .disabled(0), .enable("false")) multiplexer_7 (
    .in0(Input[8]), .in1(Input[9]), .in2(Input[10]), .in3(Input[11]), .in4(Input[12]), .in5(Input[13]),
    .in6(Input[14]), .in7(1'b0), .in8(1'b0), .in9(1'b0), .in10(1'b0), .in11(1'b0), .in12(1'b0), .in13(1'b0),
    .in14(1'b0), .in15(1'b0), .in16(1'b0), .in17(1'b0), .in18(1'b0), .in19(1'b0), .in20(1'b0), .in21(1'b0),
    .in22(1'b0), .in23(1'b0), .in24(1'b0), .in25(1'b0), .in26(1'b0), .in27(1'b0), .in28(1'b0), .in29(1'b0),
    .in30(1'b0), .in31(1'b0), .out(Output[8]), .sel(Shift_Amount));
  Multiplexer #(.select(5), .disabled(0), .enable("false")) multiplexer_8 (
    .in0(Input[7]), .in1(Input[8]), .in2(Input[9]), .in3(Input[10]), .in4(Input[11]), .in5(Input[12]),
    .in6(Input[13]), .in7(Input[14]), .in8(1'b0), .in9(1'b0), .in10(1'b0), .in11(1'b0), .in12(1'b0),
    .in13(1'b0), .in14(1'b0), .in15(1'b0), .in16(1'b0), .in17(1'b0), .in18(1'b0), .in19(1'b0), .in20(1'b0),
    .in21(1'b0), .in22(1'b0), .in23(1'b0), .in24(1'b0), .in25(1'b0), .in26(1'b0), .in27(1'b0), .in28(1'b0),
    .in29(1'b0), .in30(1'b0), .in31(1'b0), .out(Output[7]), .sel(Shift_Amount));
  Multiplexer #(.select(5), .disabled(0), .enable("false")) multiplexer_9 (
    .in0(Input[6]), .in1(Input[7]), .in2(Input[8]), .in3(Input[9]), .in4(Input[10]), .in5(Input[11]),
    .in6(Input[12]), .in7(Input[13]), .in8(Input[14]), .in9(1'b0), .in10(1'b0), .in11(1'b0), .in12(1'b0),
    .in13(1'b0), .in14(1'b0), .in15(1'b0), .in16(1'b0), .in17(1'b0), .in18(1'b0), .in19(1'b0), .in20(1'b0),
    .in21(1'b0), .in22(1'b0), .in23(1'b0), .in24(1'b0), .in25(1'b0), .in26(1'b0), .in27(1'b0), .in28(1'b0),
    .in29(1'b0), .in30(1'b0), .in31(1'b0), .out(Output[6]), .sel(Shift_Amount));
  Multiplexer #(.select(5), .disabled(0), .enable("false")) multiplexer_10 (
    .in0(Input[5]), .in1(Input[6]), .in2(Input[7]), .in3(Input[8]), .in4(Input[9]), .in5(Input[10]),
    .in6(Input[11]), .in7(Input[12]), .in8(Input[13]), .in9(Input[14]), .in10(1'b0), .in11(1'b0),
    .in12(1'b0), .in13(1'b0), .in14(1'b0), .in15(1'b0), .in16(1'b0), .in17(1'b0), .in18(1'b0), .in19(1'b0),
    .in20(1'b0), .in21(1'b0), .in22(1'b0), .in23(1'b0), .in24(1'b0), .in25(1'b0), .in26(1'b0), .in27(1'b0),
    .in28(1'b0), .in29(1'b0), .in30(1'b0), .in31(1'b0), .out(Output[5]), .sel(Shift_Amount));
  Multiplexer #(.select(5), .disabled(0), .enable("false")) multiplexer_11 (
    .in0(Input[4]), .in1(Input[5]), .in2(Input[6]), .in3(Input[7]), .in4(Input[8]), .in5(Input[9]),
    .in6(Input[10]), .in7(Input[11]), .in8(Input[12]), .in9(Input[13]), .in10(Input[14]), .in11(1'b0),
    .in12(1'b0), .in13(1'b0), .in14(1'b0), .in15(1'b0), .in16(1'b0), .in17(1'b0), .in18(1'b0), .in19(1'b0),
    .in20(1'b0), .in21(1'b0), .in22(1'b0), .in23(1'b0), .in24(1'b0), .in25(1'b0), .in26(1'b0), .in27(1'b0),
    .in28(1'b0), .in29(1'b0), .in30(1'b0), .in31(1'b0), .out(Output[4]), .sel(Shift_Amount));
  Multiplexer #(.select(5), .disabled(0), .enable("false")) multiplexer_12 (
    .in0(Input[3]), .in1(Input[4]), .in2(Input[5]), .in3(Input[6]), .in4(Input[7]), .in5(Input[8]),
    .in6(Input[9]), .in7(Input[10]), .in8(Input[11]), .in9(Input[12]), .in10(Input[13]), .in11(Input[14]),
    .in12(1'b0), .in13(1'b0), .in14(1'b0), .in15(1'b0), .in16(1'b0), .in17(1'b0), .in18(1'b0), .in19(1'b0),
    .in20(1'b0), .in21(1'b0), .in22(1'b0), .in23(1'b0), .in24(1'b0), .in25(1'b0), .in26(1'b0), .in27(1'b0),
    .in28(1'b0), .in29(1'b0), .in30(1'b0), .in31(1'b0), .out(Output[3]), .sel(Shift_Amount));
  Multiplexer #(.select(5), .disabled(0), .enable("false")) multiplexer_13 (
    .in0(Input[2]), .in1(Input[3]), .in2(Input[4]), .in3(Input[5]), .in4(Input[6]), .in5(Input[7]),
    .in6(Input[8]), .in7(Input[9]), .in8(Input[10]), .in9(Input[11]), .in10(Input[12]), .in11(Input[13]),
    .in12(Input[14]), .in13(1'b0), .in14(1'b0), .in15(1'b0), .in16(1'b0), .in17(1'b0), .in18(1'b0),
    .in19(1'b0), .in20(1'b0), .in21(1'b0), .in22(1'b0), .in23(1'b0), .in24(1'b0), .in25(1'b0), .in26(1'b0),
    .in27(1'b0), .in28(1'b0), .in29(1'b0), .in30(1'b0), .in31(1'b0), .out(Output[2]), .sel(Shift_Amount));
  Multiplexer #(.select(5), .disabled(0), .enable("false")) multiplexer_14 (
    .in0(Input[1]), .in1(Input[2]), .in2(Input[3]), .in3(Input[4]), .in4(Input[5]), .in5(Input[6]),
    .in6(Input[7]), .in7(Input[8]), .in8(Input[9]), .in9(Input[10]), .in10(Input[11]), .in11(Input[12]),
    .in12(Input[13]), .in13(Input[14]), .in14(1'b0), .in15(1'b0), .in16(1'b0), .in17(1'b0), .in18(1'b0),
    .in19(1'b0), .in20(1'b0), .in21(1'b0), .in22(1'b0), .in23(1'b0), .in24(1'b0), .in25(1'b0), .in26(1'b0),
    .in27(1'b0), .in28(1'b0), .in29(1'b0), .in30(1'b0), .in31(1'b0), .out(Output[1]), .sel(Shift_Amount));
  or or_1 (or_1_out, Input[0], Input[1]);
  or or_2 (or_2_out, or_1_out, Input[2]);
  or or_3 (or_3_out, or_2_out, Input[3]);
  or or_4 (or_4_out, or_3_out, Input[4]);
  or or_5 (or_5_out, or_4_out, Input[5]);
  or or_6 (or_6_out, or_5_out, Input[6]);
  or or_7 (or_7_out, or_6_out, Input[7]);
  or or_8 (or_8_out, or_7_out, Input[8]);
  or or_9 (or_9_out, or_8_out, Input[9]);
  or or_10 (or_10_out, or_9_out, Input[10]);
  or or_11 (or_11_out, or_10_out, Input[11]);
  or or_12 (or_12_out, or_11_out, Input[12]);
  or or_13 (or_13_out, or_12_out, Input[13]);
  or or_14 (or_14_out, or_13_out, Input[14]);
  Multiplexer #(.select(5), .disabled(0), .enable("false")) multiplexer_15 (
    .in0(Input[0]), .in1(or_1_out), .in2(or_2_out), .in3(or_3_out), .in4(or_4_out), .in5(or_5_out),
    .in6(or_6_out), .in7(or_7_out), .in8(or_8_out), .in9(or_9_out), .in10(or_10_out), .in11(or_11_out),
    .in12(or_12_out), .in13(or_13_out), .in14(or_14_out), .in15(1'b0), .in16(1'b0), .in17(1'b0), .in18(1'b0),
    .in19(1'b0), .in20(1'b0), .in21(1'b0), .in22(1'b0), .in23(1'b0), .in24(1'b0), .in25(1'b0), .in26(1'b0),
    .in27(1'b0), .in28(1'b0), .in29(1'b0), .in30(1'b0), .in31(1'b0), .out(Output[0]), .sel(Shift_Amount));
endmodule

module Bit_inverter (
  input  Control,
  input  [14:0] Input,
  output [15:0] Output
);

  wire [15:0] xor_1_out;

  assign xor_1_out = {16{Control}} ^ {1'b0, Input};  // XOR_Gate xor_1, 16 bits wide
  Adder_part #(.width(16)) adder_1 (.a({16{1'b0}}), .b(xor_1_out), .out(Output), .cin(Control));  // open: cout
endmodule

module Control (
  input  Sign_A,
  input  Sign_B,
  input  Add_prime_Sub,
  output Invert
);

  ExactlyOne xor_1 (.out(Invert), .in0(Sign_A), .in1(Sign_B), .in2(Add_prime_Sub));
endmodule

module Adder (
  input  [15:0] Input_A,
  input  [15:0] Input_B,
  output [15:0] Output
);

  Adder_part #(.width(16)) adder_1 (.a(Input_A), .b(Input_B), .out(Output), .cin(1'b0));  // open: cout
endmodule

module Bit_Finder (
  input  [15:0] Input,
  output [4:0] Position,
  output Present
);

  wire [3:0] bitfinder_1_index;

  BitFinder #(.width(16)) bitfinder_1 (
    .in({Input[0], Input[1], Input[2], Input[3], Input[4], Input[5], Input[6], Input[7], Input[8], Input[9], Input[10], Input[11], Input[12], Input[13], Input[14], Input[15]}),
    .index(bitfinder_1_index), .found(Present));
  Subtractor #(.width(5)) subtractor_1 (
    .a({bitfinder_1_index, 1'b0}), .b({5{1'b0}}), .out(Position), .bin(1'b1));  // open: bout
endmodule

module Shifter (
  input  [15:0] Input,
  input  [4:0] Shift_Amount,
  output [15:0] Output
);

  wire [15:0] shifter_1_out;

  Shifter_part #(.width(16), .shift("rl")) shifter_1 (
    .in(Input), .\dist (Shift_Amount[4:1]), .out({shifter_1_out[15], Output[14:1], shifter_1_out[0]}));
  or or_1 (Output[0], shifter_1_out[0], shifter_1_out[15]);

  assign Output[15] = 1'b0;
endmodule

module Sign_Control (
  input  Sign_A,
  input  Sign_B,
  input  Add_Sub,
  input  Number_A___Number_B,
  output Output_Sign
);

  wire xor_1_out;

  xor xor_1 (xor_1_out, Sign_B, Add_Sub);
  Multiplexer #(.disabled(0), .enable("false")) multiplexer_1 (
    .in0(Sign_A), .in1(xor_1_out), .out(Output_Sign), .sel(Number_A___Number_B));
endmodule

module Normalizing_Hardware (
  input  [4:0] Exponent_In,
  input  [15:0] Significant_In,
  output [4:0] Exponent_Out,
  output [15:0] Significant_Out
);

  wire and_1_out, bit_finder_1_present, nand_1_out, nand_2_out, nor_1_out, or_1_out, subtractor_1_bout;
  wire [4:0] bit_finder_1_position, multiplexer_2_out, subtractor_1_out, subtractor_2_out;
  wire [15:0] shifter_1_output;

  Multiplexer #(.width(5), .disabled(0), .enable("false")) multiplexer_1 (
    .in0(subtractor_1_out), .in1({5{1'b0}}), .out(Exponent_Out), .sel(and_1_out));
  Subtractor #(.width(5)) subtractor_1 (
    .a(Exponent_In), .b(bit_finder_1_position), .out(subtractor_1_out), .bin(1'b0), .bout(subtractor_1_bout));
  nor nor_1 (nor_1_out, subtractor_1_out[0], subtractor_1_out[1], subtractor_1_out[2], subtractor_1_out[3], subtractor_1_out[4]);
  or or_1 (or_1_out, subtractor_1_bout, nor_1_out);
  nand nand_1 (nand_1_out, bit_finder_1_position[0], bit_finder_1_position[1], bit_finder_1_position[2], bit_finder_1_position[3], bit_finder_1_position[4], bit_finder_1_present);
  Bit_Finder bit_finder_1 (.Input(Significant_In), .Position(bit_finder_1_position), .Present(bit_finder_1_present));
  and and_1 (and_1_out, or_1_out, nand_1_out);
  nand nand_2 (nand_2_out, Exponent_Out[0], Exponent_Out[1], Exponent_Out[2], Exponent_Out[3], Exponent_Out[4]);
  Subtractor #(.width(5)) subtractor_2 (
    .a(Exponent_In), .b({5{1'b0}}), .out(subtractor_2_out), .bin(1'b1));  // open: bout
  Multiplexer #(.width(5), .disabled(0), .enable("false")) multiplexer_2 (
    .in0(bit_finder_1_position), .in1(subtractor_2_out), .out(multiplexer_2_out), .sel(and_1_out));
  Shifter shifter_1 (.Input(Significant_In), .Shift_Amount(multiplexer_2_out), .Output(shifter_1_output));
  Multiplexer #(.width(16), .disabled(0), .enable("false")) multiplexer_3 (
    .in0(16'h4000), .in1(shifter_1_output), .out(Significant_Out), .sel(nand_2_out));
  // AND_Gate and_2 is placed but not wired
endmodule

module Special_Case_Handler (
  input  Add_prime_Sub,
  input  [15:0] Number_A,
  input  [15:0] Number_B,
  output Enable,
  output [15:0] Number_Sum
);

  wire xor_2_out;
  wire [1:0] and_1_out, or_2_out;
  wire [15:0] multiplexer_2_out, multiplexer_3_out;
  wire [15:15] xor_1_out;

  or or_1 (Enable, and_1_out[0], and_1_out[1]);
  and and_1 (and_1_out[0], Number_A[14], Number_A[13], Number_A[12], Number_A[11]);
  or or_2 (or_2_out[0], Number_A[10], Number_A[9], Number_A[8], Number_A[7], Number_A[6], Number_A[5], Number_A[4], Number_A[3], Number_A[2], Number_A[1], Number_A[0]);
  xor xor_1 (xor_1_out[15], Add_prime_Sub, Number_B[15]);
  Multiplexer #(.select(2), .width(16), .disabled(0), .enable("false")) multiplexer_1 (
    .in0(Number_A), .in1(Number_A), .in2({xor_1_out[15], Number_B[14:0]}), .in3(multiplexer_2_out),
    .out(Number_Sum), .sel(and_1_out));
  and and_2 (and_1_out[1], Number_B[14], Number_B[13], Number_B[12], Number_B[11]);
  xor xor_2 (xor_2_out, xor_1_out[15], Number_A[15]);
  or or_3 (or_2_out[1], Number_B[10], Number_B[9], Number_B[8], Number_B[7], Number_B[6], Number_B[5], Number_B[4], Number_B[3], Number_B[2], Number_B[1], Number_B[0]);
  Multiplexer #(.select(2), .width(16), .disabled(0), .enable("false")) multiplexer_2 (
    .in0(multiplexer_3_out), .in1(Number_A), .in2({xor_1_out[15], Number_B[14:0]}), .in3(Number_A),
    .out(multiplexer_2_out), .sel(or_2_out));
  Multiplexer #(.width(16), .disabled(0), .enable("false")) multiplexer_3 (
    .in0({xor_1_out[15], Number_B[14:0]}), .in1({16{1'b1}}), .out(multiplexer_3_out), .sel(xor_2_out));
endmodule

module Floating_Point_Adder (
  input  Add_prime_Sub,
  input  [15:0] Number_A,
  input  [15:0] Number_B,
  output [15:0] Number_Sum
);

  wire compare_1_number_a___number_b, control_1_invert, special_case_handler_1_enable;
  wire [4:0] compare_1_exponent_difference, multiplexer_1_out, normalizing_hardware_1_exponent_out,
       padder_1_exponent_out, padder_2_exponent_out, rounding_hardware_2_1_exponent_out;
  wire [14:0] multiplexer_3_out, multiplexer_4_out, padder_1_significant, padder_2_significant,
       right_shifter_1_output;
  wire [15:0] adder_1_output, bit_extender_1_out, bit_inverter_1_output,
       normalizing_hardware_1_significant_out, rounding_hardware_2_1_fraction_out,
       special_case_handler_1_number_sum;

  Sign_Control sign_control_1 (
    .Sign_A(Number_A[15]), .Sign_B(Number_B[15]), .Number_A___Number_B(compare_1_number_a___number_b),
    .Output_Sign(rounding_hardware_2_1_fraction_out[15]), .Add_Sub(Add_prime_Sub));
  Multiplexer #(.width(5), .disabled(0), .enable("false")) multiplexer_1 (
    .in0(padder_1_exponent_out), .in1(padder_2_exponent_out), .out(multiplexer_1_out),
    .sel(compare_1_number_a___number_b));
  Control control_1 (
    .Sign_A(Number_A[15]), .Sign_B(Number_B[15]), .Invert(control_1_invert), .Add_prime_Sub(Add_prime_Sub));
  Padder padder_1 (
    .Exponent_In(Number_A[14:10]), .Fraction(Number_A[9:0]), .Exponent_Out(padder_1_exponent_out),
    .Significant(padder_1_significant));
  Rounding_Hardware_2 rounding_hardware_2_1 (
    .Exponent_In(normalizing_hardware_1_exponent_out),
    .Significant_In(normalizing_hardware_1_significant_out),
    .Exponent_Out(rounding_hardware_2_1_exponent_out), .Fraction_Out(rounding_hardware_2_1_fraction_out[9:0]));
  Compare compare_1 (
    .Fraction_A(Number_A[9:0]), .Exponent_A(Number_A[14:10]), .Fraction_B(Number_B[9:0]),
    .Exponent_B(Number_B[14:10]), .Exponent_Difference(compare_1_exponent_difference),
    .Number_A___Number_B(compare_1_number_a___number_b));
  Normalizing_Hardware normalizing_hardware_1 (
    .Exponent_In(multiplexer_1_out), .Significant_In(adder_1_output),
    .Exponent_Out(normalizing_hardware_1_exponent_out),
    .Significant_Out(normalizing_hardware_1_significant_out));
  Multiplexer #(.width(16), .disabled(0), .enable("false")) multiplexer_2 (
    .in0({rounding_hardware_2_1_fraction_out[15], rounding_hardware_2_1_exponent_out, rounding_hardware_2_1_fraction_out[9:0]}),
    .in1(special_case_handler_1_number_sum), .out(Number_Sum), .sel(special_case_handler_1_enable));
  Multiplexer #(.width(15), .disabled(0), .enable("false")) multiplexer_3 (
    .in0(padder_1_significant), .in1(padder_2_significant), .out(multiplexer_3_out),
    .sel(compare_1_number_a___number_b));
  Padder padder_2 (
    .Exponent_In(Number_B[14:10]), .Fraction(Number_B[9:0]), .Exponent_Out(padder_2_exponent_out),
    .Significant(padder_2_significant));
  Multiplexer #(.width(15), .disabled(0), .enable("false")) multiplexer_4 (
    .in0(padder_2_significant), .in1(padder_1_significant), .out(multiplexer_4_out),
    .sel(compare_1_number_a___number_b));
  assign bit_extender_1_out = {{1{1'b0}}, multiplexer_3_out};  // Bit_Extender bit_extender_1
  Right_Shifter right_shifter_1 (
    .Shift_Amount(compare_1_exponent_difference), .Output(right_shifter_1_output), .Input(multiplexer_4_out));
  Bit_inverter bit_inverter_1 (
    .Control(control_1_invert), .Input(right_shifter_1_output), .Output(bit_inverter_1_output));
  Adder adder_1 (.Input_A(bit_inverter_1_output), .Input_B(bit_extender_1_out), .Output(adder_1_output));
  Special_Case_Handler special_case_handler_1 (
    .Number_A(Number_A), .Number_B(Number_B), .Enable(special_case_handler_1_enable),
    .Number_Sum(special_case_handler_1_number_sum), .Add_prime_Sub(Add_prime_Sub));
endmodule

module Compare (
  input  [9:0] Fraction_A,
  input  [4:0] Exponent_A,
  input  [9:0] Fraction_B,
  input  [4:0] Exponent_B,
  output [4:0] Exponent_Difference,
  output Number_A___Number_B
);

  wire nor_1_out, nor_2_out, subtractor_1_bout;
  wire [0:0] multiplexer_1_out, multiplexer_2_out;
  wire [4:0] negator_1_out, subtractor_1_out;

  Multiplexer #(.disabled(0), .enable("false")) multiplexer_1 (
    .in0(Exponent_A[0]), .in1(nor_1_out), .out(multiplexer_1_out[0]), .sel(nor_1_out));
  Multiplexer #(.disabled(0), .enable("false")) multiplexer_2 (
    .in0(Exponent_B[0]), .in1(nor_2_out), .out(multiplexer_2_out[0]), .sel(nor_2_out));
  Comparator #(.width(15), .mode("unsigned")) comparator_1 (
    .a({Exponent_A, Fraction_A}), .b({Exponent_B, Fraction_B}), .lt(Number_A___Number_B));  // open: gt, eq
  nor nor_1 (nor_1_out, Exponent_A[1], Exponent_A[2], Exponent_A[0], Exponent_A[3], Exponent_A[4]);
  Subtractor #(.width(5)) subtractor_1 (
    .a({Exponent_A[4:1], multiplexer_1_out[0]}), .b({Exponent_B[4:1], multiplexer_2_out[0]}),
    .out(subtractor_1_out), .bin(1'b0), .bout(subtractor_1_bout));
  nor nor_2 (nor_2_out, Exponent_B[3], Exponent_B[2], Exponent_B[4], Exponent_B[1], Exponent_B[0]);
  Negator #(.width(5)) negator_1 (.in(subtractor_1_out), .out(negator_1_out));
  Multiplexer #(.width(5), .disabled(0), .enable("false")) multiplexer_3 (
    .in0(subtractor_1_out), .in1(negator_1_out), .out(Exponent_Difference), .sel(subtractor_1_bout));
endmodule

module Padder (
  input  [4:0] Exponent_In,
  input  [9:0] Fraction,
  output [4:0] Exponent_Out,
  output [14:0] Significant
);

  Multiplexer #(.width(5), .disabled(0), .enable("false")) multiplexer_1 (
    .in0(5'b00001), .in1(Exponent_In), .out(Exponent_Out), .sel(Significant[14]));
  or or_1 (Significant[14], Exponent_In[4], Exponent_In[3], Exponent_In[2], Exponent_In[1], Exponent_In[0]);

  assign Significant[13:0] = {Fraction, 4'b0000};
endmodule

module Rounding_Hardware (
  input  [4:0] Exponent_In,
  input  [15:0] Significant_In,
  output [4:0] Exponent_Out,
  output [10:0] Fraction_Out
);

  wire and_1_out, or_1_out;
  wire [0:0] adder_2_out_2;
  wire [1:0] shifter_1_out;
  wire [4:0] adder_1_out, multiplexer_1_out;
  wire [11:0] adder_2_out;

  Multiplexer #(.width(5), .disabled(0), .enable("false")) multiplexer_1 (
    .in0({5{1'b0}}), .in1(Exponent_In), .out(multiplexer_1_out), .sel(adder_2_out[11]));
  Multiplexer #(.width(5), .disabled(0), .enable("false")) multiplexer_2 (
    .in0(multiplexer_1_out), .in1(adder_1_out), .out(Exponent_Out), .sel(adder_2_out_2[0]));
  Adder_part #(.width(5)) adder_1 (.a(Exponent_In), .b({5{1'b0}}), .out(adder_1_out), .cin(1'b1));  // open: cout
  and and_1 (and_1_out, Significant_In[1], or_1_out);
  or or_1 (or_1_out, Significant_In[2], Significant_In[0]);
  Adder_part #(.width(13)) adder_2 (
    .a(Significant_In[15:3]), .b({13{1'b0}}), .out({adder_2_out_2[0], adder_2_out}), .cin(and_1_out));  // open: cout
  Shifter_part #(.width(13), .shift("lr")) shifter_1 (
    .in({adder_2_out_2[0], adder_2_out}), .\dist ({3'b000, adder_2_out_2[0]}),
    .out({shifter_1_out, Fraction_Out}));
endmodule

module Rounding_Hardware_2 (
  input  [4:0] Exponent_In,
  input  [15:0] Significant_In,
  output [9:0] Fraction_Out,
  output [4:0] Exponent_Out
);

  wire adder_2_cout, and_1_out, or_1_out;
  wire [0:0] adder_2_out;

  Adder_part #(.width(5)) adder_1 (
    .a(Exponent_In), .b({5{1'b0}}), .out(Exponent_Out), .cin(adder_2_cout));  // open: cout
  or or_1 (or_1_out, Significant_In[15], Significant_In[14], Significant_In[13], Significant_In[12], Significant_In[10]);
  and and_1 (and_1_out, or_1_out, Significant_In[11]);
  Adder_part #(.width(11)) adder_2 (
    .a(Significant_In[10:0]), .b({11{1'b0}}), .out({Fraction_Out, adder_2_out[0]}), .cin(and_1_out),
    .cout(adder_2_cout));
endmodule
